// Logisim project AND.circ as structural Verilog: 1 circuit, main circuit main
module main (
  input  [15:0] R1,
  input  [15:0] R2,
  output [15:0] Re
);

  and and_1 (Re[0], R1[0], R2[0]);
  and and_2 (Re[1], R1[1], R2[1]);
  and and_3 (Re[2], R1[2], R2[2]);
  and and_4 (Re[3], R1[3], R2[3]);
  and and_5 (Re[4], R1[4], R2[4]);
  and and_6 (Re[5], R1[5], R2[5]);
  and and_7 (Re[6], R1[6], R2[6]);
  and and_8 (Re[7], R1[7], R2[7]);
  and and_9 (Re[8], R1[8], R2[8]);
  and and_10 (Re[9], R1[9], R2[9]);
  and and_11 (Re[10], R1[10], R2[10]);
  and and_12 (Re[11], R1[11], R2[11]);
  and and_13 (Re[12], R1[12], R2[12]);
  and and_14 (Re[13], R1[13], R2[13]);
  and and_15 (Re[14], R1[14], R2[14]);
  and and_16 (Re[15], R1[15], R2[15]);
endmodule
