// Logisim project JMP.circ as structural Verilog: 1 circuit, main circuit main
module main (
  input  [3:0] Opcode,
  input  [3:0] R1,
  input  [3:0] R2,
  input  Bbit,
  input  [15:0] Res2,
  input  [15:0] PC,
  output [15:0] Imm,
  output Jact,
  output [15:0] PCdata
);

  wire and_1_out, demultiplexer_1_out12, demultiplexer_1_out13, demultiplexer_1_out14, demultiplexer_1_out15;

  and and_1 (and_1_out, demultiplexer_1_out13, Bbit);
  Demultiplexer #(.select(4), .enable("false")) demultiplexer_1 (
    .out12(demultiplexer_1_out12), .out13(demultiplexer_1_out13), .out14(demultiplexer_1_out14),
    .out15(demultiplexer_1_out15), .in(1'b1), .sel(Opcode));  // open: out0, out1, out2, out3, out4, out5, out6, out7, out8, out9, out10, out11
  assign Imm = demultiplexer_1_out12 ? {{8{1'b0}}, R2, R1} : 16'bz;  // Controlled_Buffer controlled_buffer_1
  assign Jact = demultiplexer_1_out12 ? 1'b1 : 1'bz;  // Controlled_Buffer controlled_buffer_2
  assign Jact = demultiplexer_1_out14 ? 1'b1 : 1'bz;  // Controlled_Buffer controlled_buffer_3
  assign Imm = and_1_out ? {{8{1'b0}}, R2, R1} : 16'bz;  // Controlled_Buffer controlled_buffer_4
  assign Jact = and_1_out ? 1'b1 : 1'bz;  // Controlled_Buffer controlled_buffer_5
  assign Imm = demultiplexer_1_out14 ? Res2 : 16'bz;  // Controlled_Buffer controlled_buffer_6
  assign PCdata = demultiplexer_1_out15 ? PC : 16'bz;  // Controlled_Buffer controlled_buffer_7
endmodule
