// Logisim project MEM.circ as structural Verilog: 3 circuits, main circuit main
module main (
  input  [3:0] Opcode,
  input  [3:0] R1,
  input  [3:0] R2,
  input  [15:0] Direccion_R2,
  input  [15:0] Guardar_R1,
  input  [15:0] Redest,
  output [15:0] Resultado,
  output [15:0] Address_R2,
  output ActR,
  output [15:0] Store_R1
);

  wire demultiplexer_1_out8, demultiplexer_1_out9, demultiplexer_1_out10, demultiplexer_1_out11;
  wire [15:0] li_1_result, lui_1_result;

  LI li_1 (.Rdc1(R1), .Rdc2(R2), .Result(li_1_result));
  LUI lui_1 (.Rdc1(R1), .Rdc2(R2), .Result(lui_1_result));
  assign Address_R2 = demultiplexer_1_out8 ? Direccion_R2 : 16'bz;  // Controlled_Buffer controlled_buffer_1
  assign ActR = demultiplexer_1_out8 ? 1'b1 : 1'bz;  // Controlled_Buffer controlled_buffer_2
  assign Store_R1 = demultiplexer_1_out8 ? Guardar_R1 : 16'bz;  // Controlled_Buffer controlled_buffer_3
  assign Resultado = demultiplexer_1_out10 ? li_1_result : 16'bz;  // Controlled_Buffer controlled_buffer_4
  assign Resultado = demultiplexer_1_out11 ? lui_1_result : 16'bz;  // Controlled_Buffer controlled_buffer_5
  assign ActR = demultiplexer_1_out9 ? 1'b0 : 1'bz;  // Controlled_Buffer controlled_buffer_6
  assign Address_R2 = demultiplexer_1_out9 ? Direccion_R2 : 16'bz;  // Controlled_Buffer controlled_buffer_7
  assign Resultado = demultiplexer_1_out9 ? Redest : 16'bz;  // Controlled_Buffer controlled_buffer_8
  Demultiplexer #(.select(4), .enable("false")) demultiplexer_1 (
    .out8(demultiplexer_1_out8), .out9(demultiplexer_1_out9), .out10(demultiplexer_1_out10),
    .out11(demultiplexer_1_out11), .in(1'b1), .sel(Opcode));  // open: out0, out1, out2, out3, out4, out5, out6, out7, out12, out13, out14, out15
endmodule

module LI (
  input  [3:0] Rdc1,
  input  [3:0] Rdc2,
  output [15:0] Result
);


  assign Result = {{8{1'b0}}, Rdc1, Rdc2};
endmodule

module LUI (
  input  [3:0] Rdc1,
  input  [3:0] Rdc2,
  output [15:0] Result
);


  assign Result = {Rdc1, Rdc2, {8{1'b0}}};
endmodule
