// Logisim project Procesador16Bits.circ as structural Verilog: 5 circuits, main circuit main
module main (
);

  wire alu_1_bbit, Bbit, button_1_out, clock_1_out, Jact, mem_1_actr, not_1_out, not_2_out, Reset_All_out;
  wire [3:0] rom_1_data_2, rom_1_data_3;
  wire [7:0] rom_1_data;
  wire [15:0] counter_1_q, Imm, mem_1_address_r2, mem_1_store_r1, PC_DATA, R1, R2, Rdest;

  Hex_Digit_Display hex_digit_display_1 (.value(rom_1_data_3));  // open: dp
  Hex_Digit_Display hex_digit_display_2 (.value(rom_1_data_2));  // open: dp
  Hex_Digit_Display hex_digit_display_3 (.value(rom_1_data[7:4]));  // open: dp
  Hex_Digit_Display hex_digit_display_4 (.value(rom_1_data[3:0]));  // open: dp
  not not_1 (not_1_out, Jact);
  Clock clock_1 (.out(clock_1_out));
  Counter #(.width(16), .max('hffff)) counter_1 (
    .load(Jact), .D(Imm), .count(not_1_out), .Q(counter_1_q), .clk(clock_1_out), .clr(button_1_out));  // open: carry
  Button button_1 (.out(button_1_out));
  JMP jmp_1 (
    .Opcode(rom_1_data_3), .R1(rom_1_data[3:0]), .R2(rom_1_data[7:4]), .Bbit(Bbit), .Res2(R2),
    .PC(counter_1_q), .Imm(Imm), .Jact(Jact), .PCdata(PC_DATA));
  ROM #(.addrWidth(16), .dataWidth(16)) rom_1 (
    .addr(counter_1_q), .data({rom_1_data_3, rom_1_data_2, rom_1_data}));  // open: sel
  MEM mem_1 (
    .Opcode(rom_1_data_3), .R1(rom_1_data[7:4]), .R2(rom_1_data[3:0]), .Direccion_R2(R2), .Guardar_R1(R1),
    .Redest(Rdest), .Resultado(PC_DATA), .Address_R2(mem_1_address_r2), .ActR(mem_1_actr),
    .Store_R1(mem_1_store_r1));
  D_Flip_Flop d_ff_1 (.clk(clock_1_out), .D(alu_1_bbit), .Q(Bbit));  // open: Qn, preset, en, reset
  ALU alu_1 (.RN1(R1), .RN2(R2), .OP(rom_1_data_3), .result(PC_DATA), .Bbit(alu_1_bbit));
  RAM #(.addrWidth(16), .dataWidth(16), .bus("separate")) ram_1 (
    .addr(mem_1_address_r2), .din(mem_1_store_r1), .data(Rdest), .str(mem_1_actr), .clk(clock_1_out),
    .ld(not_2_out), .clr(Reset_All_out));  // open: sel
  not not_2 (not_2_out, mem_1_actr);
  Button Reset_All (.out(Reset_All_out));
  REG reg_1 (
    .RC1(rom_1_data[3:0]), .RC2(rom_1_data[7:4]), .DataR(PC_DATA), .RegN(rom_1_data_2), .Clock(clock_1_out),
    .Rsrc1(R1), .Rsrc2(R2));

  // Notes on the sheet:
  //   Current Instruction
  //   contents of rom_1 (hex, n*v repeats v):
  //   aa00 ab01 a000 a150 a207 a680 2316 703a d00a a301 371a 5170 a400 a8fe 371a 2178 374a 5470 1532 60a5
  //   d018 374a 47b 335a 370a 7b a808 7008 d027 383a 5380 2816 708a d024 373a 37b 371a 5170 c00d c027
endmodule

module JMP (
  input  [3:0] Opcode,
  input  [3:0] R1,
  input  [3:0] R2,
  input  Bbit,
  input  [15:0] Res2,
  input  [15:0] PC,
  output [15:0] Imm,
  output Jact,
  output [15:0] PCdata
);

  wire and_1_out, demultiplexer_1_out12, demultiplexer_1_out13, demultiplexer_1_out14, demultiplexer_1_out15;

  and and_1 (and_1_out, demultiplexer_1_out13, Bbit);
  Demultiplexer #(.select(4), .enable("false")) demultiplexer_1 (
    .out12(demultiplexer_1_out12), .out13(demultiplexer_1_out13), .out14(demultiplexer_1_out14),
    .out15(demultiplexer_1_out15), .in(1'b1), .sel(Opcode));  // open: out0, out1, out2, out3, out4, out5, out6, out7, out8, out9, out10, out11
  assign Imm = demultiplexer_1_out12 ? {{8{1'b0}}, R2, R1} : 16'bz;  // Controlled_Buffer controlled_buffer_1
  assign Jact = demultiplexer_1_out12 ? 1'b1 : 1'bz;  // Controlled_Buffer controlled_buffer_2
  assign Jact = demultiplexer_1_out14 ? 1'b1 : 1'bz;  // Controlled_Buffer controlled_buffer_3
  assign Imm = and_1_out ? {{8{1'b0}}, R2, R1} : 16'bz;  // Controlled_Buffer controlled_buffer_4
  assign Jact = and_1_out ? 1'b1 : 1'bz;  // Controlled_Buffer controlled_buffer_5
  assign Imm = demultiplexer_1_out14 ? Res2 : 16'bz;  // Controlled_Buffer controlled_buffer_6
  assign PCdata = demultiplexer_1_out15 ? PC : 16'bz;  // Controlled_Buffer controlled_buffer_7
endmodule

module ALU (
  input  [15:0] RN1,
  input  [15:0] RN2,
  input  [3:0] OP,
  output [15:0] result,
  output Bbit
);

  wire demultiplexer_1_out0, demultiplexer_1_out1, demultiplexer_1_out2, demultiplexer_1_out3,
       demultiplexer_1_out4, demultiplexer_1_out5, demultiplexer_1_out6, demultiplexer_1_out7, slt_1_bbit,
       undriven;
  wire [15:0] add_1_result, and_1_re, or_1_re, sl_1_result, sr_1_result, sub_1_out_3;

  ADD add_1 (.B(RN1), .A(RN2), .Result(add_1_result));  // open: out_4
  SUB sub_1 (.S(RN1), .M(RN2), .out_3(sub_1_out_3));  // open: Borrow
  AND and_1 (.R1(RN1), .R2(RN2), .Re(and_1_re));
  OR or_1 (.R1(RN1), .R2(RN2), .Re(or_1_re));
  SR sr_1 (.N1(RN2), .Result(sr_1_result));  // open: Overflow
  SL sl_1 (.N1(RN2), .Result(sl_1_result));  // open: Overflow
  SLT slt_1 (.N1(RN1), .N2(RN2), .Bbit(slt_1_bbit));
  CMP cmp_1 (.N1(RN1), .N2(RN2));  // open: Branchbit
  assign result = demultiplexer_1_out0 ? add_1_result : 16'bz;  // Controlled_Buffer controlled_buffer_1
  assign result = demultiplexer_1_out1 ? sub_1_out_3 : 16'bz;  // Controlled_Buffer controlled_buffer_2
  assign result = demultiplexer_1_out2 ? and_1_re : 16'bz;  // Controlled_Buffer controlled_buffer_3
  assign result = demultiplexer_1_out3 ? or_1_re : 16'bz;  // Controlled_Buffer controlled_buffer_4
  assign result = demultiplexer_1_out4 ? sr_1_result : 16'bz;  // Controlled_Buffer controlled_buffer_5
  assign result = demultiplexer_1_out5 ? sl_1_result : 16'bz;  // Controlled_Buffer controlled_buffer_6
  assign Bbit = demultiplexer_1_out6 ? slt_1_bbit : 1'bz;  // Controlled_Buffer controlled_buffer_7
  assign Bbit = demultiplexer_1_out7 ? undriven : 1'bz;  // Controlled_Buffer controlled_buffer_8
  Demultiplexer #(.select(4), .enable("false")) demultiplexer_1 (
    .out0(demultiplexer_1_out0), .out1(demultiplexer_1_out1), .out2(demultiplexer_1_out2),
    .out3(demultiplexer_1_out3), .out4(demultiplexer_1_out4), .out5(demultiplexer_1_out5),
    .out6(demultiplexer_1_out6), .out7(demultiplexer_1_out7), .in(1'b1), .sel(OP));  // open: out8, out9, out10, out11, out12, out13, out14, out15
endmodule

module MEM (
  input  [3:0] Opcode,
  input  [3:0] R1,
  input  [3:0] R2,
  input  [15:0] Direccion_R2,
  input  [15:0] Guardar_R1,
  input  [15:0] Redest,
  output [15:0] Resultado,
  output [15:0] Address_R2,
  output ActR,
  output [15:0] Store_R1
);

  wire demultiplexer_1_out8, demultiplexer_1_out9, demultiplexer_1_out10, demultiplexer_1_out11;
  wire [15:0] li_1_result, lui_1_result;

  LI li_1 (.Rdc1(R1), .Rdc2(R2), .Result(li_1_result));
  LUI lui_1 (.Rdc1(R1), .Rdc2(R2), .Result(lui_1_result));
  assign Address_R2 = demultiplexer_1_out8 ? Direccion_R2 : 16'bz;  // Controlled_Buffer controlled_buffer_1
  assign ActR = demultiplexer_1_out8 ? 1'b1 : 1'bz;  // Controlled_Buffer controlled_buffer_2
  assign Store_R1 = demultiplexer_1_out8 ? Guardar_R1 : 16'bz;  // Controlled_Buffer controlled_buffer_3
  assign Resultado = demultiplexer_1_out10 ? li_1_result : 16'bz;  // Controlled_Buffer controlled_buffer_4
  assign Resultado = demultiplexer_1_out11 ? lui_1_result : 16'bz;  // Controlled_Buffer controlled_buffer_5
  assign ActR = demultiplexer_1_out9 ? 1'b0 : 1'bz;  // Controlled_Buffer controlled_buffer_6
  assign Address_R2 = demultiplexer_1_out9 ? Direccion_R2 : 16'bz;  // Controlled_Buffer controlled_buffer_7
  assign Resultado = demultiplexer_1_out9 ? Redest : 16'bz;  // Controlled_Buffer controlled_buffer_8
  Demultiplexer #(.select(4), .enable("false")) demultiplexer_1 (
    .out8(demultiplexer_1_out8), .out9(demultiplexer_1_out9), .out10(demultiplexer_1_out10),
    .out11(demultiplexer_1_out11), .in(1'b1), .sel(Opcode));  // open: out0, out1, out2, out3, out4, out5, out6, out7, out12, out13, out14, out15
endmodule

// Regs
module REG (
  input  [3:0] RC1,
  input  [3:0] RC2,
  input  [15:0] DataR,
  input  [3:0] RegN,
  input  Clock,
  output [15:0] Rsrc1,
  output [15:0] Rsrc2
);

  wire demultiplexer_1_out0, demultiplexer_1_out1, demultiplexer_1_out2, demultiplexer_1_out3,
       demultiplexer_1_out4, demultiplexer_1_out5, demultiplexer_1_out6, demultiplexer_1_out7,
       demultiplexer_1_out8, demultiplexer_1_out9, demultiplexer_1_out10, demultiplexer_1_out11,
       demultiplexer_1_out12, demultiplexer_1_out13, demultiplexer_1_out14, demultiplexer_1_out15;
  wire [15:0] register_1_q, register_2_q, register_3_q, register_4_q, register_5_q, register_6_q,
       register_7_q, register_8_q, register_9_q, register_10_q, register_11_q, register_12_q, register_13_q,
       register_14_q, register_15_q, register_16_q;

  Demultiplexer #(.select(4), .enable("false")) demultiplexer_1 (
    .out0(demultiplexer_1_out0), .out1(demultiplexer_1_out1), .out2(demultiplexer_1_out2),
    .out3(demultiplexer_1_out3), .out4(demultiplexer_1_out4), .out5(demultiplexer_1_out5),
    .out6(demultiplexer_1_out6), .out7(demultiplexer_1_out7), .out8(demultiplexer_1_out8),
    .out9(demultiplexer_1_out9), .out10(demultiplexer_1_out10), .out11(demultiplexer_1_out11),
    .out12(demultiplexer_1_out12), .out13(demultiplexer_1_out13), .out14(demultiplexer_1_out14),
    .out15(demultiplexer_1_out15), .in(1'b1), .sel(RegN));
  Register #(.width(16)) register_1 (.D(DataR), .en(demultiplexer_1_out0), .Q(register_1_q), .clk(Clock));  // open: clr
  Register #(.width(16)) register_2 (.D(DataR), .en(demultiplexer_1_out1), .Q(register_2_q), .clk(Clock));  // open: clr
  Register #(.width(16)) register_3 (.D(DataR), .en(demultiplexer_1_out2), .Q(register_3_q), .clk(Clock));  // open: clr
  Register #(.width(16)) register_4 (.D(DataR), .en(demultiplexer_1_out3), .Q(register_4_q), .clk(Clock));  // open: clr
  Register #(.width(16)) register_5 (.D(DataR), .en(demultiplexer_1_out4), .Q(register_5_q), .clk(Clock));  // open: clr
  Register #(.width(16)) register_6 (.D(DataR), .en(demultiplexer_1_out5), .Q(register_6_q), .clk(Clock));  // open: clr
  Register #(.width(16)) register_7 (.D(DataR), .en(demultiplexer_1_out6), .Q(register_7_q), .clk(Clock));  // open: clr
  Register #(.width(16)) register_8 (.D(DataR), .en(demultiplexer_1_out7), .Q(register_8_q), .clk(Clock));  // open: clr
  Register #(.width(16)) register_9 (.D(DataR), .en(demultiplexer_1_out8), .Q(register_9_q), .clk(Clock));  // open: clr
  Register #(.width(16)) register_10 (
    .D(DataR), .en(demultiplexer_1_out9), .Q(register_10_q), .clk(Clock));  // open: clr
  Register #(.width(16)) register_11 (
    .D(DataR), .en(demultiplexer_1_out10), .Q(register_11_q), .clk(Clock));  // open: clr
  Register #(.width(16)) register_12 (
    .D(DataR), .en(demultiplexer_1_out11), .Q(register_12_q), .clk(Clock));  // open: clr
  Register #(.width(16)) register_13 (
    .D(DataR), .en(demultiplexer_1_out12), .Q(register_13_q), .clk(Clock));  // open: clr
  Register #(.width(16)) register_14 (
    .D(DataR), .en(demultiplexer_1_out13), .Q(register_14_q), .clk(Clock));  // open: clr
  Register #(.width(16)) register_15 (
    .D(DataR), .en(demultiplexer_1_out14), .Q(register_15_q), .clk(Clock));  // open: clr
  Register #(.width(16)) register_16 (.D(DataR), .en(demultiplexer_1_out15), .Q(register_16_q));  // open: clk, clr
  Multiplexer #(.select(4), .width(16), .enable("false")) multiplexer_1 (
    .in0(register_1_q), .in1(register_2_q), .in2(register_3_q), .in3(register_4_q), .in4(register_5_q),
    .in5(register_6_q), .in6(register_7_q), .in7(register_8_q), .in8(register_9_q), .in9(register_10_q),
    .in10(register_11_q), .in11(register_12_q), .in12(register_13_q), .in13(register_14_q),
    .in14(register_15_q), .in15(register_16_q), .out(Rsrc1), .sel(RC1));
  Multiplexer #(.select(4), .width(16), .enable("false")) multiplexer_2 (
    .in0(register_1_q), .in1(register_2_q), .in2(register_3_q), .in3(register_4_q), .in4(register_5_q),
    .in5(register_6_q), .in6(register_7_q), .in7(register_8_q), .in8(register_9_q), .in9(register_10_q),
    .in10(register_11_q), .in11(register_12_q), .in12(register_13_q), .in13(register_14_q),
    .in14(register_15_q), .in15(register_16_q), .out(Rsrc2), .sel(RC2));

  // Notes on the sheet:
  //   R0
  //   R1
  //   R2
  //   R3
  //   R4
  //   R5
  //   R6
  //   R7
  //   R8
  //   R9
  //   R10
  //   R11
  //   R12
  //   R13
  //   R14
  //   R15
endmodule
