// Logisim project dañado.circ as structural Verilog: 15 circuits, main circuit main
module main (
  output [15:0] \Instrucción 
);

  wire alu_1_bbit, Bbit, button_1_out, clock_1_out, Jact_1, mem_1_actr, not_1_out, not_2_out, Reset_out;
  wire [15:0] Imm_16, jmp_1_p4, mem_1_address_r2, mem_1_store_r1, PCData, R1, R2, Rdest;

  Button button_1 (.out(button_1_out));
  not not_1 (not_1_out, Jact_1);
  // JMP jmp_1: pin names not known; wires that end beside it: PCData, Jact_1, Imm_16, jmp_1_p4, \Instrucción [15:12], R2, Bbit, \Instrucción [7:4], \Instrucción [3:0]
  Counter #(.width(16), .max('hffff)) PC (
    .load(Jact_1), .D(Imm_16), .count(not_1_out), .Q(jmp_1_p4), .clk(clock_1_out), .clr(button_1_out));  // open: carry
  Clock clock_1 (.out(clock_1_out));
  MEM mem_1 (
    .Opcode(\Instrucción [3:0]), .R1(\Instrucción [3:0]), .R2(\Instrucción [7:4]), .Direccion_R2(R1),
    .Guardar_R1(R2), .Redest(Rdest), .Address_R2(mem_1_address_r2), .ActR(mem_1_actr),
    .Store_R1(mem_1_store_r1), .Resultado(PCData));
  ROM #(.addrWidth(16), .dataWidth(16)) rom_1 (.addr(jmp_1_p4), .data(\Instrucción ));  // open: sel
  ALU alu_1 (.RN1(R1), .RN2(R2), .OP(\Instrucción [15:12]), .result(PCData), .Bbit(alu_1_bbit));
  REGISTERS registers_1 (
    .RC1(\Instrucción [3:0]), .RC2(\Instrucción [7:4]), .DataR(PCData), .RegN(\Instrucción [11:8]),
    .Clock(clock_1_out), .Rsrc1(R1), .Rsrc2(R2));
  RAM #(.addrWidth(16), .dataWidth(16), .bus("separate")) ram_1 (
    .addr(mem_1_address_r2), .din(mem_1_store_r1), .data(Rdest), .str(mem_1_actr), .clk(clock_1_out),
    .ld(not_2_out), .clr(Reset_out));  // open: sel
  not not_2 (not_2_out, mem_1_actr);
  Button Reset (.out(Reset_out));
  D_Flip_Flop d_ff_1 (.clk(clock_1_out), .D(alu_1_bbit), .Q(Bbit));  // open: Qn, preset, en, reset

  // Notes on the sheet:
  //   PROCESADOR DE 16 BITS
  //   PROFESOR SERRACIN
  //   Memoria de Instrucciones
  //   contents of rom_1 (hex, n*v repeats v):
  //   a401 a507 145 8011 9810 a305 8033 434 9230 7023 a801 d00f 4*0 3778 a809 4778
  //   RAM
endmodule

module ADD (
  input  [15:0] A,
  input  [15:0] B,
  output [15:0] Result,
  output out_4
);

  wire and_1_out, and_2_out, and_3_out, and_4_out, and_5_out, and_6_out, and_7_out, and_8_out, and_9_out,
       and_10_out, and_11_out, and_12_out, and_13_out, and_14_out, and_15_out, and_16_out, and_17_out,
       and_18_out, and_19_out, and_20_out, and_21_out, and_22_out, and_23_out, and_24_out, and_25_out,
       and_26_out, and_27_out, and_28_out, and_29_out, and_30_out, and_31_out, and_32_out, C_2_out, C_3_out,
       C_4_out, C_5_out, C_6_out, C_7_out, C_8_out, C_9_out, C_10_out, C_11_out, C_12_out, C_13_out,
       C_15_out, C_16_out, C_out, xor_1_out, xor_2_out, xor_3_out, xor_4_out, xor_5_out, xor_6_out,
       xor_7_out, xor_8_out, xor_9_out, xor_10_out, xor_11_out, xor_12_out, xor_13_out, xor_14_out,
       xor_15_out, xor_16_out;

  and and_1 (and_1_out, A[0], B[0]);
  and and_2 (and_2_out, A[1], B[1]);
  and and_3 (and_3_out, A[2], B[2]);
  and and_4 (and_4_out, A[4], B[4]);
  and and_5 (and_5_out, A[5], B[5]);
  and and_6 (and_6_out, A[7], B[7]);
  and and_7 (and_7_out, A[8], B[8]);
  and and_8 (and_8_out, A[9], B[9]);
  and and_9 (and_9_out, A[10], B[10]);
  and and_10 (and_10_out, A[11], B[11]);
  and and_11 (and_11_out, A[12], B[12]);
  and and_12 (and_12_out, A[13], B[13]);
  and and_13 (and_13_out, A[14], B[14]);
  and and_14 (and_14_out, A[15], B[15]);
  xor xor_1 (xor_1_out, A[0], B[0]);
  xor xor_2 (xor_2_out, A[1], B[1]);
  xor xor_3 (xor_3_out, A[2], B[2]);
  xor xor_4 (xor_4_out, A[3], B[3]);
  and and_15 (and_15_out, A[3], B[3]);
  xor xor_5 (xor_5_out, A[4], B[4]);
  xor xor_6 (xor_6_out, A[5], B[5]);
  xor xor_7 (xor_7_out, A[6], B[6]);
  and and_16 (and_16_out, A[6], B[6]);
  xor xor_8 (xor_8_out, A[7], B[7]);
  xor xor_9 (xor_9_out, A[8], B[8]);
  xor xor_10 (xor_10_out, A[9], B[9]);
  xor xor_11 (xor_11_out, A[10], B[10]);
  xor xor_12 (xor_12_out, A[11], B[11]);
  xor xor_13 (xor_13_out, A[12], B[12]);
  xor xor_14 (xor_14_out, A[13], B[13]);
  xor xor_15 (xor_15_out, A[14], B[14]);
  xor xor_16 (xor_16_out, A[15], B[15]);
  xor xor_17 (Result[0], xor_1_out, 1'b0);
  and and_17 (and_17_out, xor_1_out, 1'b0);
  or C (C_out, and_17_out, and_1_out);
  xor xor_18 (Result[1], xor_2_out, C_out);
  and and_18 (and_18_out, xor_2_out, C_out);
  or C_2 (C_2_out, and_18_out, and_2_out);
  xor xor_19 (Result[2], xor_3_out, C_2_out);
  and and_19 (and_19_out, xor_3_out, C_2_out);
  or C_3 (C_3_out, and_19_out, and_3_out);
  xor xor_20 (Result[3], xor_4_out, C_3_out);
  and and_20 (and_20_out, xor_4_out, C_3_out);
  xor xor_21 (Result[4], xor_5_out, C_15_out);
  and and_21 (and_21_out, xor_5_out, C_15_out);
  or C_4 (C_4_out, and_21_out, and_4_out);
  xor xor_22 (Result[5], xor_6_out, C_4_out);
  or C_5 (C_5_out, and_22_out, and_5_out);
  and and_22 (and_22_out, xor_6_out, C_4_out);
  xor xor_23 (Result[6], xor_7_out, C_5_out);
  and and_23 (and_23_out, xor_7_out, C_5_out);
  xor xor_24 (Result[7], xor_8_out, C_16_out);
  or C_6 (C_6_out, and_24_out, and_6_out);
  and and_24 (and_24_out, xor_8_out, C_16_out);
  xor xor_25 (Result[8], xor_9_out, C_6_out);
  and and_25 (and_25_out, xor_9_out, C_6_out);
  or C_7 (C_7_out, and_25_out, and_7_out);
  xor xor_26 (Result[9], xor_10_out, C_7_out);
  and and_26 (and_26_out, xor_10_out, C_7_out);
  or C_8 (C_8_out, and_26_out, and_8_out);
  xor xor_27 (Result[10], xor_11_out, C_8_out);
  or C_9 (C_9_out, and_27_out, and_9_out);
  and and_27 (and_27_out, xor_11_out, C_8_out);
  xor xor_28 (Result[11], xor_12_out, C_9_out);
  and and_28 (and_28_out, xor_12_out, C_9_out);
  or C_10 (C_10_out, and_28_out, and_10_out);
  xor xor_29 (Result[12], xor_13_out, C_10_out);
  or C_11 (C_11_out, and_29_out, and_11_out);
  and and_29 (and_29_out, xor_13_out, C_10_out);
  xor xor_30 (Result[13], xor_14_out, C_11_out);
  and and_30 (and_30_out, xor_14_out, C_11_out);
  or C_12 (C_12_out, and_30_out, and_12_out);
  xor xor_31 (Result[14], xor_15_out, C_12_out);
  or C_13 (C_13_out, and_31_out, and_13_out);
  and and_31 (and_31_out, xor_15_out, C_12_out);
  xor xor_32 (Result[15], xor_16_out, C_13_out);
  or C_14 (out_4, and_32_out, and_14_out);
  and and_32 (and_32_out, xor_16_out, C_13_out);
  or C_15 (C_15_out, and_20_out, and_15_out);
  or C_16 (C_16_out, and_23_out, and_16_out);
endmodule

module SUB (
  input  [15:0] M,
  input  [15:0] S,
  output [15:0] out_3,
  output Borrow
);

  wire and_1_out, and_2_out, and_3_out, and_4_out, and_5_out, and_6_out, and_7_out, and_8_out, and_9_out,
       and_10_out, and_11_out, and_12_out, and_13_out, and_14_out, and_15_out, and_16_out, and_17_out,
       and_18_out, and_19_out, and_20_out, and_21_out, and_22_out, and_23_out, and_24_out, and_25_out,
       and_26_out, and_27_out, and_28_out, and_29_out, and_30_out, and_31_out, and_32_out, B_2_out, B_3_out,
       B_4_out, B_5_out, B_6_out, B_7_out, B_8_out, B_9_out, B_10_out, B_11_out, B_12_out, B_13_out,
       B_14_out, B_15_out, B_out, not_1_out, not_2_out, not_3_out, not_4_out, not_5_out, not_6_out,
       not_7_out, not_8_out, not_9_out, not_10_out, not_11_out, not_12_out, not_13_out, not_14_out,
       not_15_out, not_16_out, not_17_out, not_18_out, not_19_out, not_20_out, not_21_out, not_22_out,
       not_23_out, not_24_out, not_25_out, not_26_out, not_27_out, not_28_out, not_29_out, not_30_out,
       not_31_out, not_32_out, xor_1_out, xor_2_out, xor_3_out, xor_4_out, xor_5_out, xor_6_out, xor_7_out,
       xor_8_out, xor_9_out, xor_10_out, xor_11_out, xor_12_out, xor_13_out, xor_14_out, xor_15_out,
       xor_16_out;

  not not_1 (not_1_out, M[12]);
  not not_2 (not_2_out, M[13]);
  not not_3 (not_3_out, M[14]);
  not not_4 (not_4_out, M[15]);
  not not_5 (not_5_out, M[4]);
  not not_6 (not_6_out, M[5]);
  not not_7 (not_7_out, M[6]);
  not not_8 (not_8_out, M[7]);
  not not_9 (not_9_out, M[8]);
  not not_10 (not_10_out, M[9]);
  not not_11 (not_11_out, M[10]);
  not not_12 (not_12_out, M[11]);
  not not_13 (not_13_out, M[0]);
  not not_14 (not_14_out, M[1]);
  not not_15 (not_15_out, M[2]);
  not not_16 (not_16_out, M[3]);
  xor xor_1 (xor_1_out, M[0], S[0]);
  and and_1 (and_1_out, not_13_out, S[0]);
  xor xor_2 (xor_2_out, M[1], S[1]);
  and and_2 (and_2_out, not_14_out, S[1]);
  xor xor_3 (xor_3_out, M[2], S[2]);
  and and_3 (and_3_out, not_15_out, S[2]);
  xor xor_4 (xor_4_out, M[3], S[3]);
  and and_4 (and_4_out, not_16_out, S[3]);
  xor xor_5 (xor_5_out, M[4], S[4]);
  and and_5 (and_5_out, not_5_out, S[4]);
  xor xor_6 (xor_6_out, M[5], S[5]);
  and and_6 (and_6_out, not_6_out, S[5]);
  xor xor_7 (xor_7_out, M[6], S[6]);
  and and_7 (and_7_out, not_7_out, S[6]);
  xor xor_8 (xor_8_out, M[7], S[7]);
  and and_8 (and_8_out, not_8_out, S[7]);
  xor xor_9 (xor_9_out, M[8], S[8]);
  and and_9 (and_9_out, not_9_out, S[8]);
  xor xor_10 (xor_10_out, M[9], S[9]);
  and and_10 (and_10_out, not_10_out, S[9]);
  xor xor_11 (xor_11_out, M[10], S[10]);
  and and_11 (and_11_out, not_11_out, S[10]);
  xor xor_12 (xor_12_out, M[11], S[11]);
  and and_12 (and_12_out, not_12_out, S[11]);
  xor xor_13 (xor_13_out, M[12], S[12]);
  and and_13 (and_13_out, not_1_out, S[12]);
  xor xor_14 (xor_14_out, M[13], S[13]);
  and and_14 (and_14_out, not_2_out, S[13]);
  xor xor_15 (xor_15_out, M[14], S[14]);
  and and_15 (and_15_out, not_3_out, S[14]);
  xor xor_16 (xor_16_out, M[15], S[15]);
  and and_16 (and_16_out, not_4_out, S[15]);
  xor T (out_3[0], xor_1_out, 1'b0);
  not not_17 (not_17_out, xor_1_out);
  and and_17 (and_17_out, not_17_out, 1'b0);
  xor xor_17 (out_3[1], xor_2_out, B_out);
  not not_18 (not_18_out, xor_2_out);
  and and_18 (and_18_out, not_18_out, B_out);
  xor xor_18 (out_3[2], xor_3_out, B_2_out);
  not not_19 (not_19_out, xor_3_out);
  and and_19 (and_19_out, not_19_out, B_2_out);
  xor xor_19 (out_3[3], xor_4_out, B_3_out);
  not not_20 (not_20_out, xor_4_out);
  and and_20 (and_20_out, not_20_out, B_3_out);
  xor xor_20 (out_3[4], xor_5_out, B_4_out);
  not not_21 (not_21_out, xor_5_out);
  and and_21 (and_21_out, not_21_out, B_4_out);
  xor xor_21 (out_3[5], xor_6_out, B_5_out);
  not not_22 (not_22_out, xor_6_out);
  and and_22 (and_22_out, not_22_out, B_5_out);
  xor xor_22 (out_3[6], xor_7_out, B_6_out);
  not not_23 (not_23_out, xor_7_out);
  and and_23 (and_23_out, not_23_out, B_6_out);
  xor xor_23 (out_3[7], xor_8_out, B_7_out);
  not not_24 (not_24_out, xor_8_out);
  and and_24 (and_24_out, not_24_out, B_7_out);
  xor xor_24 (out_3[8], xor_9_out, B_8_out);
  not not_25 (not_25_out, xor_9_out);
  and and_25 (and_25_out, not_25_out, B_8_out);
  xor xor_25 (out_3[9], xor_10_out, B_9_out);
  not not_26 (not_26_out, xor_10_out);
  and and_26 (and_26_out, not_26_out, B_9_out);
  xor xor_26 (out_3[10], xor_11_out, B_10_out);
  not not_27 (not_27_out, xor_11_out);
  and and_27 (and_27_out, not_27_out, B_10_out);
  xor xor_27 (out_3[11], xor_12_out, B_11_out);
  not not_28 (not_28_out, xor_12_out);
  and and_28 (and_28_out, not_28_out, B_11_out);
  xor xor_28 (out_3[12], xor_13_out, B_12_out);
  not not_29 (not_29_out, xor_13_out);
  and and_29 (and_29_out, not_29_out, B_12_out);
  xor xor_29 (out_3[13], xor_14_out, B_13_out);
  not not_30 (not_30_out, xor_14_out);
  and and_30 (and_30_out, not_30_out, B_13_out);
  xor xor_30 (out_3[14], xor_15_out, B_14_out);
  not not_31 (not_31_out, xor_15_out);
  and and_31 (and_31_out, not_31_out, B_14_out);
  xor xor_31 (out_3[15], xor_16_out, B_15_out);
  not not_32 (not_32_out, xor_16_out);
  and and_32 (and_32_out, not_32_out, B_15_out);
  or B (B_out, and_17_out, and_1_out);
  or B_2 (B_2_out, and_18_out, and_2_out);
  or B_3 (B_3_out, and_19_out, and_3_out);
  or B_4 (B_4_out, and_20_out, and_4_out);
  or B_5 (B_5_out, and_21_out, and_5_out);
  or B_6 (B_6_out, and_22_out, and_6_out);
  or B_7 (B_7_out, and_7_out, and_23_out);
  or B_8 (B_8_out, and_8_out, and_24_out);
  or B_9 (B_9_out, and_9_out, and_25_out);
  or B_10 (B_10_out, and_10_out, and_26_out);
  or B_11 (B_11_out, and_11_out, and_27_out);
  or B_12 (B_12_out, and_12_out, and_28_out);
  or B_13 (B_13_out, and_13_out, and_29_out);
  or B_14 (B_14_out, and_14_out, and_30_out);
  or B_15 (B_15_out, and_15_out, and_31_out);
  or B_16 (Borrow, and_16_out, and_32_out);
endmodule

module AND (
  input  [15:0] R1,
  input  [15:0] R2,
  output [15:0] Re
);

  and and_1 (Re[0], R1[0], R2[0]);
  and and_2 (Re[1], R1[1], R2[1]);
  and and_3 (Re[2], R1[2], R2[2]);
  and and_4 (Re[3], R1[3], R2[3]);
  and and_5 (Re[4], R1[4], R2[4]);
  and and_6 (Re[5], R1[5], R2[5]);
  and and_7 (Re[6], R1[6], R2[6]);
  and and_8 (Re[7], R1[7], R2[7]);
  and and_9 (Re[8], R1[8], R2[8]);
  and and_10 (Re[9], R1[9], R2[9]);
  and and_11 (Re[10], R1[10], R2[10]);
  and and_12 (Re[11], R1[11], R2[11]);
  and and_13 (Re[12], R1[12], R2[12]);
  and and_14 (Re[13], R1[13], R2[13]);
  and and_15 (Re[14], R1[14], R2[14]);
  and and_16 (Re[15], R1[15], R2[15]);
endmodule

module OR (
  input  [15:0] R1,
  input  [15:0] R2,
  output [15:0] Re
);

  or or_1 (Re[0], R1[0], R2[0]);
  or or_2 (Re[1], R1[1], R2[1]);
  or or_3 (Re[2], R1[2], R2[2]);
  or or_4 (Re[3], R1[3], R2[3]);
  or or_5 (Re[4], R1[4], R2[4]);
  or or_6 (Re[5], R1[5], R2[5]);
  or or_7 (Re[6], R1[6], R2[6]);
  or or_8 (Re[7], R1[7], R2[7]);
  or or_9 (Re[8], R1[8], R2[8]);
  or or_10 (Re[9], R1[9], R2[9]);
  or or_11 (Re[10], R1[10], R2[10]);
  or or_12 (Re[11], R1[11], R2[11]);
  or or_13 (Re[12], R1[12], R2[12]);
  or or_14 (Re[13], R1[13], R2[13]);
  or or_15 (Re[14], R1[14], R2[14]);
  or or_16 (Re[15], R1[15], R2[15]);
endmodule

module XOR (
  input  [15:0] R1,
  input  [15:0] R2,
  output [15:0] Re
);

  xor xor_1 (Re[0], R1[0], R2[0]);
  xor xor_2 (Re[1], R1[1], R2[1]);
  xor xor_3 (Re[2], R1[2], R2[2]);
  xor xor_4 (Re[3], R1[3], R2[3]);
  xor xor_5 (Re[4], R1[4], R2[4]);
  xor xor_6 (Re[5], R1[5], R2[5]);
  xor xor_7 (Re[6], R1[6], R2[6]);
  xor xor_8 (Re[7], R1[7], R2[7]);
  xor xor_9 (Re[8], R1[8], R2[8]);
  xor xor_10 (Re[9], R1[9], R2[9]);
  xor xor_11 (Re[10], R1[10], R2[10]);
  xor xor_12 (Re[11], R1[11], R2[11]);
  xor xor_13 (Re[12], R1[12], R2[12]);
  xor xor_14 (Re[13], R1[13], R2[13]);
  xor xor_15 (Re[14], R1[14], R2[14]);
  xor xor_16 (Re[15], R1[15], R2[15]);
endmodule

// SHL
module SL (
  input  [15:0] N1,
  output [15:0] Result,
  output Overflow
);


  assign Overflow = N1[15];
  assign Result = {N1[14:0], 1'b0};
endmodule

module SLT (
  input  [15:0] N1,
  input  [15:0] N2,
  output Bbit
);

  Comparator #(.width(16)) comparator_1 (.a(N1), .b(N2), .lt(Bbit));  // open: gt, eq
endmodule

module CMP (
  input  [15:0] N1,
  input  [15:0] N2,
  output Branchbit
);

  wire comparator_1_eq, comparator_2_eq, comparator_3_eq, comparator_4_eq, comparator_5_eq, comparator_6_eq,
       comparator_7_eq, comparator_8_eq, comparator_9_eq, comparator_10_eq, comparator_11_eq,
       comparator_12_eq, comparator_13_eq, comparator_14_eq, comparator_15_eq, comparator_16_eq;

  Comparator #(.width(1)) comparator_1 (.a(N1[0]), .b(N2[0]), .eq(comparator_1_eq));  // open: gt, lt
  Comparator #(.width(1)) comparator_2 (.a(N1[1]), .b(N2[1]), .eq(comparator_2_eq));  // open: gt, lt
  Comparator #(.width(1)) comparator_3 (.a(N1[2]), .b(N2[2]), .eq(comparator_3_eq));  // open: gt, lt
  Comparator #(.width(1)) comparator_4 (.a(N1[3]), .b(N2[3]), .eq(comparator_4_eq));  // open: gt, lt
  Comparator #(.width(1)) comparator_5 (.a(N1[4]), .b(N2[4]), .eq(comparator_5_eq));  // open: gt, lt
  Comparator #(.width(1)) comparator_6 (.a(N1[5]), .b(N2[5]), .eq(comparator_6_eq));  // open: gt, lt
  Comparator #(.width(1)) comparator_7 (.a(N1[6]), .b(N2[6]), .eq(comparator_7_eq));  // open: gt, lt
  Comparator #(.width(1)) comparator_8 (.a(N1[7]), .b(N2[7]), .eq(comparator_8_eq));  // open: gt, lt
  Comparator #(.width(1)) comparator_9 (.a(N1[8]), .b(N2[8]), .eq(comparator_9_eq));  // open: gt, lt
  Comparator #(.width(1)) comparator_10 (.a(N1[9]), .b(N2[9]), .eq(comparator_10_eq));  // open: gt, lt
  Comparator #(.width(1)) comparator_11 (.a(N1[10]), .b(N2[10]), .eq(comparator_11_eq));  // open: gt, lt
  Comparator #(.width(1)) comparator_12 (.a(N1[11]), .b(N2[11]), .eq(comparator_12_eq));  // open: gt, lt
  Comparator #(.width(1)) comparator_13 (.a(N1[12]), .b(N2[12]), .eq(comparator_13_eq));  // open: gt, lt
  Comparator #(.width(1)) comparator_14 (.a(N1[13]), .b(N2[13]), .eq(comparator_14_eq));  // open: gt, lt
  Comparator #(.width(1)) comparator_15 (.a(N1[14]), .b(N2[14]), .eq(comparator_15_eq));  // open: gt, lt
  Comparator #(.width(1)) comparator_16 (.a(N1[15]), .b(N2[15]), .eq(comparator_16_eq));  // open: gt, lt
  and and_1 (Branchbit, comparator_1_eq, comparator_2_eq, comparator_3_eq, comparator_4_eq, comparator_5_eq, comparator_6_eq, comparator_7_eq, comparator_8_eq, comparator_9_eq, comparator_10_eq, comparator_11_eq, comparator_12_eq, comparator_13_eq, comparator_14_eq, comparator_15_eq, comparator_16_eq);
endmodule

module ALU (
  input  [15:0] RN1,
  input  [15:0] RN2,
  input  [3:0] OP,
  output [15:0] result,
  output Bbit
);

  wire demultiplexer_1_out0, demultiplexer_1_out1, demultiplexer_1_out2, demultiplexer_1_out3,
       demultiplexer_1_out4, demultiplexer_1_out5, demultiplexer_1_out6, demultiplexer_1_out7, slt_1_bbit,
       undriven;
  wire [15:0] add_1_result, and_1_re, or_1_re, sl_1_result, sub_1_out_3, xor_1_re;

  ADD add_1 (.B(RN1), .A(RN2), .Result(add_1_result));  // open: out_4
  SUB sub_1 (.S(RN1), .M(RN2), .out_3(sub_1_out_3));  // open: Borrow
  AND and_1 (.R1(RN1), .R2(RN2), .Re(and_1_re));
  OR or_1 (.R1(RN1), .R2(RN2), .Re(or_1_re));
  XOR xor_1 (.R1(RN1), .R2(RN2), .Re(xor_1_re));
  SL sl_1 (.N1(RN2), .Result(sl_1_result));  // open: Overflow
  SLT slt_1 (.N1(RN1), .N2(RN2), .Bbit(slt_1_bbit));
  CMP cmp_1 (.N1(RN1), .N2(RN2));  // open: Branchbit
  assign result = demultiplexer_1_out0 ? add_1_result : 16'bz;  // Controlled_Buffer controlled_buffer_1
  assign result = demultiplexer_1_out1 ? sub_1_out_3 : 16'bz;  // Controlled_Buffer controlled_buffer_2
  assign result = demultiplexer_1_out2 ? and_1_re : 16'bz;  // Controlled_Buffer controlled_buffer_3
  assign result = demultiplexer_1_out3 ? or_1_re : 16'bz;  // Controlled_Buffer controlled_buffer_4
  assign result = demultiplexer_1_out4 ? xor_1_re : 16'bz;  // Controlled_Buffer controlled_buffer_5
  assign result = demultiplexer_1_out5 ? sl_1_result : 16'bz;  // Controlled_Buffer controlled_buffer_6
  assign Bbit = demultiplexer_1_out6 ? slt_1_bbit : 1'bz;  // Controlled_Buffer controlled_buffer_7
  assign Bbit = demultiplexer_1_out7 ? undriven : 1'bz;  // Controlled_Buffer controlled_buffer_8
  Demultiplexer #(.select(4), .enable("false")) demultiplexer_1 (
    .out0(demultiplexer_1_out0), .out1(demultiplexer_1_out1), .out2(demultiplexer_1_out2),
    .out3(demultiplexer_1_out3), .out4(demultiplexer_1_out4), .out5(demultiplexer_1_out5),
    .out6(demultiplexer_1_out6), .out7(demultiplexer_1_out7), .in(1'b1), .sel(OP));  // open: out8, out9, out10, out11, out12, out13, out14, out15
endmodule

module JMP (
  input  [3:0] Opcode,
  input  [3:0] R1,
  input  [3:0] R2,
  input  Bbit,
  input  [15:0] Res2,
  input  [15:0] PC,
  output [15:0] Imm,
  output Jact,
  output [15:0] PCdata
);

  wire and_1_out, demultiplexer_1_out12, demultiplexer_1_out13, demultiplexer_1_out14, demultiplexer_1_out15;

  and and_1 (and_1_out, demultiplexer_1_out13, Bbit);
  Demultiplexer #(.select(4), .enable("false")) demultiplexer_1 (
    .out12(demultiplexer_1_out12), .out13(demultiplexer_1_out13), .out14(demultiplexer_1_out14),
    .out15(demultiplexer_1_out15), .in(1'b1), .sel(Opcode));  // open: out0, out1, out2, out3, out4, out5, out6, out7, out8, out9, out10, out11
  assign Imm = demultiplexer_1_out12 ? {{8{1'b0}}, R2, R1} : 16'bz;  // Controlled_Buffer controlled_buffer_1
  assign Jact = demultiplexer_1_out12 ? 1'b1 : 1'bz;  // Controlled_Buffer controlled_buffer_2
  assign Jact = demultiplexer_1_out14 ? 1'b1 : 1'bz;  // Controlled_Buffer controlled_buffer_3
  assign Imm = and_1_out ? {{8{1'b0}}, R2, R1} : 16'bz;  // Controlled_Buffer controlled_buffer_4
  assign Jact = and_1_out ? 1'b1 : 1'bz;  // Controlled_Buffer controlled_buffer_5
  assign Imm = demultiplexer_1_out14 ? Res2 : 16'bz;  // Controlled_Buffer controlled_buffer_6
  assign PCdata = demultiplexer_1_out15 ? PC : 16'bz;  // Controlled_Buffer controlled_buffer_7
endmodule

module LI (
  input  [3:0] Rdc1,
  input  [3:0] Rdc2,
  output [15:0] Result
);


  assign Result = {{8{1'b0}}, Rdc1, Rdc2};
endmodule

module LUI (
  input  [3:0] Rdc1,
  input  [3:0] Rdc2,
  output [15:0] Result
);


  assign Result = {Rdc1, Rdc2, {8{1'b0}}};
endmodule

module MEM (
  input  [3:0] Opcode,
  input  [3:0] R1,
  input  [3:0] R2,
  input  [15:0] Direccion_R2,
  input  [15:0] Guardar_R1,
  input  [15:0] Redest,
  output [15:0] Resultado,
  output [15:0] Address_R2,
  output ActR,
  output [15:0] Store_R1
);

  wire demultiplexer_1_out8, demultiplexer_1_out9, demultiplexer_1_out10, demultiplexer_1_out11;
  wire [15:0] li_1_result, lui_1_result;

  LI li_1 (.Rdc1(R1), .Rdc2(R2), .Result(li_1_result));
  LUI lui_1 (.Rdc1(R1), .Rdc2(R2), .Result(lui_1_result));
  assign Address_R2 = demultiplexer_1_out8 ? Direccion_R2 : 16'bz;  // Controlled_Buffer controlled_buffer_1
  assign ActR = demultiplexer_1_out8 ? 1'b1 : 1'bz;  // Controlled_Buffer controlled_buffer_2
  assign Store_R1 = demultiplexer_1_out8 ? Guardar_R1 : 16'bz;  // Controlled_Buffer controlled_buffer_3
  assign Resultado = demultiplexer_1_out10 ? li_1_result : 16'bz;  // Controlled_Buffer controlled_buffer_4
  assign Resultado = demultiplexer_1_out11 ? lui_1_result : 16'bz;  // Controlled_Buffer controlled_buffer_5
  assign ActR = demultiplexer_1_out9 ? 1'b0 : 1'bz;  // Controlled_Buffer controlled_buffer_6
  assign Address_R2 = demultiplexer_1_out9 ? Direccion_R2 : 16'bz;  // Controlled_Buffer controlled_buffer_7
  assign Resultado = demultiplexer_1_out9 ? Redest : 16'bz;  // Controlled_Buffer controlled_buffer_8
  Demultiplexer #(.select(4), .enable("false")) demultiplexer_1 (
    .out8(demultiplexer_1_out8), .out9(demultiplexer_1_out9), .out10(demultiplexer_1_out10),
    .out11(demultiplexer_1_out11), .in(1'b1), .sel(Opcode));  // open: out0, out1, out2, out3, out4, out5, out6, out7, out12, out13, out14, out15
endmodule

// REGS
module REGISTERS (
  input  [3:0] RC1,
  input  [3:0] RC2,
  input  [15:0] DataR,
  input  [3:0] RegN,
  input  Clock,
  output [15:0] Rsrc1,
  output [15:0] Rsrc2
);

  wire demultiplexer_1_out0, demultiplexer_1_out1, demultiplexer_1_out2, demultiplexer_1_out3,
       demultiplexer_1_out4, demultiplexer_1_out5, demultiplexer_1_out6, demultiplexer_1_out7,
       demultiplexer_1_out8, demultiplexer_1_out9, demultiplexer_1_out10, demultiplexer_1_out11,
       demultiplexer_1_out12, demultiplexer_1_out13, demultiplexer_1_out14, demultiplexer_1_out15;
  wire [15:0] and_1_out, register_1_q, register_2_q, register_3_q, register_4_q, register_5_q, register_6_q,
       register_7_q, register_8_q, register_9_q, register_10_q, register_11_q, register_12_q, register_13_q,
       register_14_q, register_15_q, register_16_q;

  Demultiplexer #(.select(4), .enable("false")) demultiplexer_1 (
    .out0(demultiplexer_1_out0), .out1(demultiplexer_1_out1), .out2(demultiplexer_1_out2),
    .out3(demultiplexer_1_out3), .out4(demultiplexer_1_out4), .out5(demultiplexer_1_out5),
    .out6(demultiplexer_1_out6), .out7(demultiplexer_1_out7), .out8(demultiplexer_1_out8),
    .out9(demultiplexer_1_out9), .out10(demultiplexer_1_out10), .out11(demultiplexer_1_out11),
    .out12(demultiplexer_1_out12), .out13(demultiplexer_1_out13), .out14(demultiplexer_1_out14),
    .out15(demultiplexer_1_out15), .in(1'b1), .sel(RegN));
  assign and_1_out = {16{1'b0}} & DataR;  // AND_Gate and_1, 16 bits wide
  Register #(.width(16)) register_1 (
    .D(and_1_out), .en(demultiplexer_1_out0), .Q(register_1_q), .clk(Clock));  // open: clr
  Register #(.width(16)) register_2 (.D(DataR), .en(demultiplexer_1_out1), .Q(register_2_q), .clk(Clock));  // open: clr
  Register #(.width(16)) register_3 (.D(DataR), .en(demultiplexer_1_out2), .Q(register_3_q), .clk(Clock));  // open: clr
  Register #(.width(16)) register_4 (.D(DataR), .en(demultiplexer_1_out3), .Q(register_4_q), .clk(Clock));  // open: clr
  Register #(.width(16)) register_5 (.D(DataR), .en(demultiplexer_1_out4), .Q(register_5_q), .clk(Clock));  // open: clr
  Register #(.width(16)) register_6 (.D(DataR), .en(demultiplexer_1_out5), .Q(register_6_q), .clk(Clock));  // open: clr
  Register #(.width(16)) register_7 (.D(DataR), .en(demultiplexer_1_out6), .Q(register_7_q), .clk(Clock));  // open: clr
  Register #(.width(16)) register_8 (.D(DataR), .en(demultiplexer_1_out7), .Q(register_8_q), .clk(Clock));  // open: clr
  Register #(.width(16)) register_9 (.D(DataR), .en(demultiplexer_1_out8), .Q(register_9_q), .clk(Clock));  // open: clr
  Register #(.width(16)) register_10 (
    .D(DataR), .en(demultiplexer_1_out9), .Q(register_10_q), .clk(Clock));  // open: clr
  Register #(.width(16)) register_11 (
    .D(DataR), .en(demultiplexer_1_out10), .Q(register_11_q), .clk(Clock));  // open: clr
  Register #(.width(16)) register_12 (
    .D(DataR), .en(demultiplexer_1_out11), .Q(register_12_q), .clk(Clock));  // open: clr
  Register #(.width(16)) register_13 (
    .D(DataR), .en(demultiplexer_1_out12), .Q(register_13_q), .clk(Clock));  // open: clr
  Register #(.width(16)) register_14 (
    .D(DataR), .en(demultiplexer_1_out13), .Q(register_14_q), .clk(Clock));  // open: clr
  Register #(.width(16)) register_15 (
    .D(DataR), .en(demultiplexer_1_out14), .Q(register_15_q), .clk(Clock));  // open: clr
  Register #(.width(16)) register_16 (.D(DataR), .en(demultiplexer_1_out15), .Q(register_16_q));  // open: clk, clr
  Multiplexer #(.select(4), .width(16), .enable("false")) multiplexer_1 (
    .in0(register_1_q), .in1(register_2_q), .in2(register_3_q), .in3(register_4_q), .in4(register_5_q),
    .in5(register_6_q), .in6(register_7_q), .in7(register_8_q), .in8(register_9_q), .in9(register_10_q),
    .in10(register_11_q), .in11(register_12_q), .in12(register_13_q), .in13(register_14_q),
    .in14(register_15_q), .in15(register_16_q), .out(Rsrc1), .sel(RC1));
  Multiplexer #(.select(4), .width(16), .enable("false")) multiplexer_2 (
    .in0(register_1_q), .in1(register_2_q), .in2(register_3_q), .in3(register_4_q), .in4(register_5_q),
    .in5(register_6_q), .in6(register_7_q), .in7(register_8_q), .in8(register_9_q), .in9(register_10_q),
    .in10(register_11_q), .in11(register_12_q), .in12(register_13_q), .in13(register_14_q),
    .in14(register_15_q), .in15(register_16_q), .out(Rsrc2), .sel(RC2));

  // Notes on the sheet:
  //   R0
  //   R1
  //   R2
  //   R3
  //   R4
  //   R5
  //   R6
  //   R7
  //   R8
  //   R9
  //   R10
  //   R11
  //   R12
  //   R13
  //   R14
  //   R15
endmodule
