// Logisim project LUI.circ as structural Verilog: 1 circuit, main circuit main
module main (
  input  [3:0] Rdc1,
  input  [3:0] Rdc2,
  output [15:0] Result
);


  assign Result = {Rdc1, Rdc2, {8{1'b0}}};
endmodule
