// Logisim project SL.circ as structural Verilog: 1 circuit, main circuit main
module main (
  input  [15:0] N1,
  output [15:0] Result,
  output Overflow
);


  assign Overflow = N1[15];
  assign Result = {N1[14:0], 1'b0};
endmodule
